// Logisim project Processor.circ as structural Verilog
module Processor (
  input  Reset,
  input  [3:0] Display_Address
);

  wire alu_1_is, alu_1_is_2, branch_unit_1_isbranchtaken, Clock, clock_1_out, control_unit_1_isbeq,
       control_unit_1_isbgt, control_unit_1_isimmediate, control_unit_1_isret, control_unit_1_isst,
       control_unit_1_isubranch, control_unit_1_iswb, flags_1_flags_e, flags_1_flags_gt;
  wire [1:0] control_unit_1_isld;
  wire [3:0] multiplexer_5_out, multiplexer_6_out, multiplexer_7_out, register_file_1_displayd_2,
       register_file_1_displayd_3, register_file_1_displayd_4, register_file_1_displayd_5;
  wire [4:0] rom_1_data_2;
  wire [12:0] control_unit_1_alusignals;
  wire [26:0] if_of_stage_1_out_5, rom_1_data;
  wire [31:0] adder_1_out, adder_2_out, adder_3_out, alu_1_aluresult, bit_extender_1_out,
       calculate_immediate_1_immx, if_of_stage_1_out_4, memory_unit_1_ldresult, multiplexer_1_out,
       multiplexer_2_out, multiplexer_3_out, multiplexer_4_out, PC_q, register_file_1_displayd,
       register_file_1_readd1, register_file_1_readd2, shifter_1_out;
  wire [31:27] if_of_stage_1_out_5_2;

  Clock clock_1 (.out(clock_1_out));
  Register #(.width(32), .trigger("falling")) PC (
    .D(multiplexer_1_out), .Q(PC_q), .clk(Clock), .clr(Reset));  // open: en
  Multiplexer #(.width(32), .enable("false")) multiplexer_1 (
    .in0(adder_1_out), .in1(multiplexer_3_out), .out(multiplexer_1_out));  // open: sel
  Adder #(.width(32)) adder_1 (.a(32'h4), .b(PC_q), .out(adder_1_out));  // open: cin, cout
  assign bit_extender_1_out = {{5{if_of_stage_1_out_5[26]}}, if_of_stage_1_out_5};  // Bit_Extender bit_extender_1
  IF_OF_STAGE if_of_stage_1 (
    .in_1(PC_q), .in_2({rom_1_data_2, rom_1_data}), .in_3(clock_1_out), .out_4(if_of_stage_1_out_4),
    .out_5({if_of_stage_1_out_5_2, if_of_stage_1_out_5}));
  Shifter #(.width(32)) shifter_1 (.in(bit_extender_1_out), .\dist (5'b00010), .out(shifter_1_out));
  ALU alu_1 (
    .A(register_file_1_readd1), .B(multiplexer_4_out), .ALUsignals(control_unit_1_alusignals),
    .aluResult(alu_1_aluresult), .is(alu_1_is), .is_2(alu_1_is_2));
  Adder #(.width(32)) adder_2 (.a(if_of_stage_1_out_4), .b(32'h4), .out(adder_2_out));  // open: cin, cout
  Multiplexer #(.select(2), .width(32), .enable("false")) multiplexer_2 (
    .in0(alu_1_aluresult), .in1(memory_unit_1_ldresult), .in2(adder_2_out), .out(multiplexer_2_out));  // open: in3, sel
  Calculate_Immediate calculate_immediate_1 (.imm(if_of_stage_1_out_5[17:0]), .immx(calculate_immediate_1_immx));
  Adder #(.width(32)) adder_3 (.a(shifter_1_out), .b(if_of_stage_1_out_4), .out(adder_3_out));  // open: cin, cout
  Multiplexer #(.width(32), .enable("false")) multiplexer_3 (
    .in0(adder_3_out), .in1(register_file_1_readd1), .out(multiplexer_3_out));  // open: sel
  Memory_Unit memory_unit_1 (
    .MAR(alu_1_aluresult), .ldResult(memory_unit_1_ldresult), .MDR(register_file_1_readd2),
    .isSt(control_unit_1_isst), .isLd(control_unit_1_isld[0]), .Clock(Clock), .Reset(Reset));
  Clock Clock_2 (.out(Clock));
  ROM #(.addrWidth(24), .dataWidth(32)) rom_1 (.addr(PC_q[25:2]), .data({rom_1_data_2, rom_1_data}));  // open: sel
  Multiplexer #(.width(32), .enable("false")) multiplexer_4 (
    .in0(register_file_1_readd2), .in1(calculate_immediate_1_immx), .out(multiplexer_4_out));  // open: sel
  Flags flags_1 (
    .isCmp(control_unit_1_alusignals[0]), .is(alu_1_is), .is_2(alu_1_is_2), .flags_GT(flags_1_flags_gt),
    .flags_E(flags_1_flags_e));
  Hex_Digit_Display hex_digit_display_1 (.value(register_file_1_displayd[31:28]));  // open: dp
  Multiplexer #(.width(4), .enable("false")) multiplexer_5 (
    .in0(rom_1_data[17:14]), .in1(rom_1_data[25:22]), .out(multiplexer_5_out));  // open: sel
  Hex_Digit_Display hex_digit_display_2 (.value(register_file_1_displayd[27:24]));  // open: dp
  Multiplexer #(.width(4), .enable("false")) multiplexer_6 (
    .in0(rom_1_data[21:18]), .in1(4'b1111), .out(multiplexer_6_out));  // open: sel
  Register_File register_file_1 (
    .ReadA1(multiplexer_6_out), .ReadA2(multiplexer_5_out), .WriteE(control_unit_1_iswb),
    .WriteD(multiplexer_2_out), .ReadD1(register_file_1_readd1), .ReadD2(register_file_1_readd2),
    .Clock(Clock), .Reset(Reset),
    .DisplayD({register_file_1_displayd[31:24], register_file_1_displayd_5, register_file_1_displayd_4, register_file_1_displayd_3, register_file_1_displayd_2, register_file_1_displayd[7:0]}),
    .DisplayA(Display_Address), .WriteA(multiplexer_7_out));
  Branch_Unit branch_unit_1 (
    .isBeq(control_unit_1_isbeq), .isUBranch(control_unit_1_isubranch), .flags_E(flags_1_flags_e),
    .isBgt(control_unit_1_isbgt), .flags_GT(flags_1_flags_gt), .isBranchTaken(branch_unit_1_isbranchtaken));
  Hex_Digit_Display hex_digit_display_3 (.value(register_file_1_displayd_4));  // open: dp
  Hex_Digit_Display hex_digit_display_4 (.value(register_file_1_displayd_5));  // open: dp
  Control_Unit control_unit_1 (
    .isSt(control_unit_1_isst), .isLd(control_unit_1_isld[0]), .isBeq(control_unit_1_isbeq),
    .isBgt(control_unit_1_isbgt), .isRet(control_unit_1_isret), .I_bit(rom_1_data[26]),
    .isImmediate(control_unit_1_isimmediate), .opcode(rom_1_data_2), .isWb(control_unit_1_iswb),
    .isUbranch(control_unit_1_isubranch), .isCall(control_unit_1_isld[1]),
    .ALUsignals(control_unit_1_alusignals));
  Hex_Digit_Display hex_digit_display_5 (.value(register_file_1_displayd_3));  // open: dp
  Hex_Digit_Display hex_digit_display_6 (.value(register_file_1_displayd_2));  // open: dp
  Multiplexer #(.width(4), .enable("false")) multiplexer_7 (
    .in0(rom_1_data[25:22]), .in1(4'b1111), .out(multiplexer_7_out));  // open: sel
  Hex_Digit_Display hex_digit_display_7 (.value(register_file_1_displayd[3:0]));  // open: dp
  Hex_Digit_Display hex_digit_display_8 (.value(register_file_1_displayd[7:4]));  // open: dp

  // Notes on the sheet:
  //   isBranchTaken
  //   pc+4
  //   branchTarget
  //   ALUsignals
  //   B
  //   pc
  //   imm
  //   offset
  //   pc
  //   branchTarget
  //   A
  //   ALU
  //   aluResult
  //   MAR
  //   Memory
  //   Unit
  //   ldResult
  //   Instruction Memory
  //   calc immx
  //   immx
  //   isRet
  //   isBranchTaken
  //   is>
  //   is=
  //   isCmp
  //   MDR
  //   isLd
  //   data
  //   contents of rom_1 (hex, n*v repeats v):
  //   4c800003 4cc00005
  //   rs2
  //   Flags
  //   isSt
  //   isLd
  //   isCall
  //   instruction
  //   rs1
  //   rd
  //   isSt
  //   Register
  //   File
  //   op1
  //   op2
  //   isImmediate
  //   flags(GT)
  //   flags(E)
  //   isRet
  //   isWb
  //   E
  //   address
  //   A
  //   data
  //   D
  //   Branch
  //   Unit
  //   opcode
  //   I bit
  //   isBeq
  //   isBgt
  //   isUBranch
  //   Display Register
  //   CONTROL
  //   UNIT
  //   isCall
  //   rd
endmodule

module Control_Unit (
  input  I_bit,
  input  [4:0] opcode,
  output isSt,
  output isLd,
  output isBeq,
  output isBgt,
  output isRet,
  output isImmediate,
  output isWb,
  output isUbranch,
  output isCall,
  output [12:0] ALUsignals
);

  wire and_6_out, and_7_out, and_8_out, and_9_out, and_10_out, and_12_out, and_13_out, nand_1_out;

  nand nand_1 (nand_1_out, opcode[0], opcode[1]);
  and and_1 (isSt, opcode[0], opcode[1], opcode[2], opcode[3], ~opcode[4]);  // AND_Gate
  and and_2 (isLd, ~opcode[0], opcode[1], opcode[2], opcode[3], ~opcode[4]);  // AND_Gate
  and and_3 (isBeq, ~opcode[0], ~opcode[1], ~opcode[2], ~opcode[3], opcode[4]);  // AND_Gate
  and and_4 (isBgt, opcode[0], ~opcode[1], ~opcode[2], ~opcode[3], opcode[4]);  // AND_Gate
  and and_5 (isRet, ~opcode[0], ~opcode[1], opcode[2], ~opcode[3], opcode[4]);  // AND_Gate
  and and_6 (and_6_out, opcode[0], ~opcode[1], opcode[2], ~opcode[4]);  // AND_Gate
  and and_7 (and_7_out, opcode[0], opcode[2], opcode[3], ~opcode[4]);  // AND_Gate
  and and_8 (and_8_out, opcode[4], nand_1_out);
  and and_9 (and_9_out, opcode[1], ~opcode[2], ~opcode[3], opcode[4]);  // AND_Gate
  and and_10 (and_10_out, ~opcode[0], ~opcode[1], opcode[2], ~opcode[3], opcode[4]);  // AND_Gate
  and and_11 (isCall, opcode[0], opcode[1], ~opcode[2], ~opcode[3], opcode[4]);  // AND_Gate
  and and_12 (and_12_out, ~opcode[0], ~opcode[1], ~opcode[2], ~opcode[3], ~opcode[4]);  // AND_Gate
  and and_13 (and_13_out, opcode[1], opcode[2], opcode[3], ~opcode[4]);  // AND_Gate
  and isSub (ALUsignals[2], opcode[0], ~opcode[1], ~opcode[2], ~opcode[3], ~opcode[4]);  // AND_Gate
  and isCmp (ALUsignals[0], opcode[0], ~opcode[1], opcode[2], ~opcode[3], ~opcode[4]);  // AND_Gate
  and isMul (ALUsignals[3], ~opcode[0], opcode[1], ~opcode[2], ~opcode[3], ~opcode[4]);  // AND_Gate
  and isDiv (ALUsignals[4], opcode[0], opcode[1], ~opcode[2], ~opcode[3], ~opcode[4]);  // AND_Gate
  and isMod (ALUsignals[5], ~opcode[0], ~opcode[1], opcode[2], ~opcode[3], ~opcode[4]);  // AND_Gate
  and isLsl (ALUsignals[7], ~opcode[0], opcode[1], ~opcode[2], opcode[3], ~opcode[4]);  // AND_Gate
  and isLsr (ALUsignals[8], opcode[0], opcode[1], ~opcode[2], opcode[3], ~opcode[4]);  // AND_Gate
  and isAsr (ALUsignals[9], ~opcode[0], ~opcode[1], opcode[2], opcode[3], ~opcode[4]);  // AND_Gate
  and isOr (ALUsignals[12], opcode[0], opcode[1], opcode[2], ~opcode[3], ~opcode[4]);  // AND_Gate
  and isAnd (ALUsignals[11], ~opcode[0], opcode[1], opcode[2], ~opcode[3], ~opcode[4]);  // AND_Gate
  and isNot (ALUsignals[10], ~opcode[0], ~opcode[1], ~opcode[2], opcode[3], ~opcode[4]);  // AND_Gate
  and isMov (ALUsignals[6], opcode[0], ~opcode[1], ~opcode[2], opcode[3], ~opcode[4]);  // AND_Gate
  or or_1 (isUbranch, and_9_out, and_10_out);
  or isAdd (ALUsignals[1], and_12_out, and_13_out);
  nor nor_1 (isWb, and_6_out, and_7_out, and_8_out);

  assign isImmediate = I_bit;

  // Notes on the sheet:
  //   op1
  //   op2
  //   op3
  //   op4
  //   op5
endmodule

module Register_File (
  input  Clock,
  input  Reset,
  input  [31:0] WriteD,
  input  [3:0] ReadA1,
  input  WriteE,
  input  [3:0] WriteA,
  input  [3:0] ReadA2,
  input  [3:0] DisplayA,
  output [31:0] ReadD1,
  output [31:0] ReadD2,
  output [31:0] DisplayD
);

  wire demultiplexer_1_out0, demultiplexer_1_out1, demultiplexer_1_out2, demultiplexer_1_out3,
       demultiplexer_1_out4, demultiplexer_1_out5, demultiplexer_1_out6, demultiplexer_1_out7,
       demultiplexer_1_out8, demultiplexer_1_out9, demultiplexer_1_out10, demultiplexer_1_out11,
       demultiplexer_1_out12, demultiplexer_1_out13, demultiplexer_1_out14, demultiplexer_1_out15,
       multiplexer_2_out, or_1_out, or_2_out;
  wire [31:0] multiplexer_1_out, r0_q, r1_q, r2_q, r3_q, r4_q, r5_q, r6_q, r7_q, r8_q, r9_q, r10_q, r11_q,
       r12_q, r13_q, r14_q, r15_q;

  Demultiplexer #(.select(4), .disabled(0), .enable("false")) demultiplexer_1 (
    .out0(demultiplexer_1_out0), .out1(demultiplexer_1_out1), .out2(demultiplexer_1_out2),
    .out3(demultiplexer_1_out3), .out4(demultiplexer_1_out4), .out5(demultiplexer_1_out5),
    .out6(demultiplexer_1_out6), .out7(demultiplexer_1_out7), .out8(demultiplexer_1_out8),
    .out9(demultiplexer_1_out9), .out10(demultiplexer_1_out10), .out11(demultiplexer_1_out11),
    .out12(demultiplexer_1_out12), .out13(demultiplexer_1_out13), .out14(demultiplexer_1_out14),
    .out15(demultiplexer_1_out15), .in(WriteE), .sel(WriteA));
  Multiplexer #(.width(32), .enable("false")) multiplexer_1 (
    .in0(WriteD), .in1(32'h3fffffc), .out(multiplexer_1_out), .sel(Reset));
  or or_1 (or_1_out, demultiplexer_1_out14, Reset);
  Multiplexer #(.enable("false")) multiplexer_2 (.in0(or_2_out), .out(multiplexer_2_out), .sel(1'b0));  // open: in1
  or or_2 (or_2_out, Clock, Reset);
  Register #(.width(32)) r0 (.D(WriteD), .en(demultiplexer_1_out0), .Q(r0_q), .clk(Clock), .clr(Reset));
  Register #(.width(32)) r1 (.D(WriteD), .en(demultiplexer_1_out1), .Q(r1_q), .clk(Clock), .clr(Reset));
  Register #(.width(32)) r2 (.D(WriteD), .en(demultiplexer_1_out2), .Q(r2_q), .clk(Clock), .clr(Reset));
  Register #(.width(32)) r3 (.D(WriteD), .en(demultiplexer_1_out3), .Q(r3_q), .clk(Clock), .clr(Reset));
  Register #(.width(32)) r4 (.D(WriteD), .en(demultiplexer_1_out4), .Q(r4_q), .clk(Clock), .clr(Reset));
  Register #(.width(32)) r5 (.D(WriteD), .en(demultiplexer_1_out5), .Q(r5_q), .clk(Clock), .clr(Reset));
  Register #(.width(32)) r6 (.D(WriteD), .en(demultiplexer_1_out6), .Q(r6_q), .clk(Clock), .clr(Reset));
  Register #(.width(32)) r7 (.D(WriteD), .en(demultiplexer_1_out7), .Q(r7_q), .clk(Clock), .clr(Reset));
  Register #(.width(32)) r8 (.D(WriteD), .en(demultiplexer_1_out8), .Q(r8_q), .clk(Clock), .clr(Reset));
  Register #(.width(32)) r9 (.D(WriteD), .en(demultiplexer_1_out9), .Q(r9_q), .clk(Clock), .clr(Reset));
  Register #(.width(32)) r10 (.D(WriteD), .en(demultiplexer_1_out10), .Q(r10_q), .clk(Clock), .clr(Reset));
  Register #(.width(32)) r11 (.D(WriteD), .en(demultiplexer_1_out11), .Q(r11_q), .clk(Clock), .clr(Reset));
  Register #(.width(32)) r12 (.D(WriteD), .en(demultiplexer_1_out12), .Q(r12_q), .clk(Clock), .clr(Reset));
  Register #(.width(32)) r13 (.D(WriteD), .en(demultiplexer_1_out13), .Q(r13_q), .clk(Clock), .clr(Reset));
  Register #(.width(32)) r14 (.D(multiplexer_1_out), .en(or_1_out), .Q(r14_q), .clk(multiplexer_2_out));  // open: clr
  Register #(.width(32)) r15 (.D(WriteD), .en(demultiplexer_1_out15), .Q(r15_q), .clk(Clock), .clr(Reset));
  Multiplexer #(.select(4), .width(32), .disabled(0), .enable("false")) multiplexer_3 (
    .in0(r0_q), .in1(r1_q), .in2(r2_q), .in3(r3_q), .in4(r4_q), .in5(r5_q), .in6(r6_q), .in7(r7_q),
    .in8(r8_q), .in9(r9_q), .in10(r10_q), .in11(r11_q), .in12(r12_q), .in13(r13_q), .in14(r14_q),
    .in15(r15_q), .out(ReadD1), .sel(ReadA1));
  Multiplexer #(.select(4), .width(32), .disabled(0), .enable("false")) multiplexer_4 (
    .in0(r0_q), .in1(r1_q), .in2(r2_q), .in3(r3_q), .in4(r4_q), .in5(r5_q), .in6(r6_q), .in7(r7_q),
    .in8(r8_q), .in9(r9_q), .in10(r10_q), .in11(r11_q), .in12(r12_q), .in13(r13_q), .in14(r14_q),
    .in15(r15_q), .out(ReadD2), .sel(ReadA2));
  Multiplexer #(.select(4), .width(32), .disabled(0), .enable("false")) multiplexer_5 (
    .in0(r0_q), .in1(r1_q), .in2(r2_q), .in3(r3_q), .in4(r4_q), .in5(r5_q), .in6(r6_q), .in7(r7_q),
    .in8(r8_q), .in9(r9_q), .in10(r10_q), .in11(r11_q), .in12(r12_q), .in13(r13_q), .in14(r14_q),
    .in15(r15_q), .out(DisplayD), .sel(DisplayA));
endmodule

module ALU (
  input  [31:0] A,
  input  [31:0] B,
  input  [12:0] ALUsignals,
  output [31:0] aluResult,
  output is,
  output is_2
);

  wire [31:0] adder_1_out, and_1_out, divider_1_out, divider_1_rem, multiplier_1_out, not_1_out, or_1_out,
       shifter_1_out, shifter_2_out, shifter_3_out, subtractor_1_out;

  Adder #(.width(32)) adder_1 (.a(A), .b(B), .out(adder_1_out));  // open: cin, cout
  Subtractor #(.width(32)) subtractor_1 (.a(A), .b(B), .out(subtractor_1_out));  // open: bin, bout
  Multiplier #(.width(32)) multiplier_1 (.a(A), .b(B), .out(multiplier_1_out));  // open: cin, cout
  Divider #(.width(32)) divider_1 (.a(A), .b(B), .out(divider_1_out), .rem(divider_1_rem));  // open: upper
  Comparator #(.width(32)) comparator_1 (.a(A), .b(B), .gt(is), .eq(is_2));  // open: lt
  Shifter #(.width(32)) shifter_1 (.in(A), .\dist (B[4:0]), .out(shifter_1_out));
  Shifter #(.width(32), .shift("lr")) shifter_2 (.in(A), .\dist (B[4:0]), .out(shifter_2_out));
  Shifter #(.width(32), .shift("ar")) shifter_3 (.in(A), .\dist (B[4:0]), .out(shifter_3_out));
  assign not_1_out = ~B;  // NOT_Gate not_1, 32 bits wide
  assign and_1_out = A & B;  // AND_Gate and_1, 32 bits wide
  assign or_1_out = A | B;  // OR_Gate or_1, 32 bits wide
  assign aluResult = ALUsignals[1] ? adder_1_out : 32'bz;  // Controlled_Buffer controlled_buffer_1
  assign aluResult = ALUsignals[2] ? subtractor_1_out : 32'bz;  // Controlled_Buffer controlled_buffer_2
  assign aluResult = ALUsignals[3] ? multiplier_1_out : 32'bz;  // Controlled_Buffer controlled_buffer_3
  assign aluResult = ALUsignals[4] ? divider_1_out : 32'bz;  // Controlled_Buffer controlled_buffer_4
  assign aluResult = ALUsignals[5] ? divider_1_rem : 32'bz;  // Controlled_Buffer controlled_buffer_5
  assign aluResult = ALUsignals[6] ? B : 32'bz;  // Controlled_Buffer controlled_buffer_6
  assign aluResult = ALUsignals[7] ? shifter_1_out : 32'bz;  // Controlled_Buffer controlled_buffer_7
  assign aluResult = ALUsignals[8] ? shifter_2_out : 32'bz;  // Controlled_Buffer controlled_buffer_8
  assign aluResult = ALUsignals[9] ? shifter_3_out : 32'bz;  // Controlled_Buffer controlled_buffer_9
  assign aluResult = ALUsignals[10] ? not_1_out : 32'bz;  // Controlled_Buffer controlled_buffer_10
  assign aluResult = ALUsignals[11] ? and_1_out : 32'bz;  // Controlled_Buffer controlled_buffer_11
  assign aluResult = ALUsignals[12] ? or_1_out : 32'bz;  // Controlled_Buffer controlled_buffer_12

  // Notes on the sheet:
  //   add
  //   sub
  //   mul
  //   div
  //   cmp
  //   lsr
  //   mod
  //   lsl
  //   asr
endmodule

module Flags (
  input  isCmp,
  input  is,
  input  is_2,
  output flags_GT,
  output flags_E
);

  D_Flip_Flop #(.trigger("high")) d_ff_1 (.clk(isCmp), .D(is), .Q(flags_GT));  // open: Qn, preset, en, reset
  D_Flip_Flop #(.trigger("high")) d_ff_2 (.clk(isCmp), .D(is_2), .Q(flags_E));  // open: Qn, preset, en, reset
endmodule

module Branch_Unit (
  input  isUBranch,
  input  isBeq,
  input  flags_E,
  input  isBgt,
  input  flags_GT,
  output isBranchTaken
);

  wire and_1_out, and_2_out;

  and and_1 (and_1_out, isBeq, flags_E);
  and and_2 (and_2_out, isBgt, flags_GT);
  or or_1 (isBranchTaken, isUBranch, and_1_out, and_2_out);
endmodule

module Memory_Unit (
  input  [31:0] MAR,
  input  isLd,
  input  [31:0] MDR,
  input  isSt,
  input  Clock,
  input  Reset,
  output [31:0] ldResult
);

  RAM #(.addrWidth(24), .dataWidth(32), .bus("separate")) ram_1 (
    .addr(MAR[25:2]), .din(MDR), .data(ldResult), .str(isSt), .clk(Clock), .ld(isLd), .clr(Reset));  // open: sel
endmodule

module Calculate_Immediate (
  input  [17:0] imm,
  output [31:0] immx
);

  wire [31:0] bit_extender_1_out, bit_extender_2_out, shifter_1_out;

  assign bit_extender_1_out = {{16{1'b0}}, imm[15:0]};  // Bit_Extender bit_extender_1
  assign bit_extender_2_out = {{16{imm[15]}}, imm[15:0]};  // Bit_Extender bit_extender_2
  Shifter #(.width(32)) shifter_1 (.in(bit_extender_1_out), .\dist (5'b10000), .out(shifter_1_out));
  Multiplexer #(.select(2), .width(32), .enable("false")) multiplexer_1 (
    .in0(bit_extender_2_out), .in1(bit_extender_1_out), .in2(shifter_1_out), .out(immx), .sel(imm[17:16]));  // open: in3

  // Notes on the sheet:
  //   modifier bits
  //   high
  //   default
  //   unsigned
endmodule

module IF_OF_STAGE (
  input  [31:0] in_1,
  input  [31:0] in_2,
  input  in_3,
  output [31:0] out_4,
  output [31:0] out_5
);

  Register #(.width(32)) PC (.D(in_1), .Q(out_4), .clk(in_3));  // open: en, clr
  Register #(.width(32)) INSTRUCTION (.D(in_2), .Q(out_5), .clk(in_3));  // open: en, clr
endmodule

// Pipeline
module PipeLine (
  input  Reset,
  input  Data_Lock,
  input  [3:0] Display_Address,
  output [31:0] out_4,
  output [31:0] Display
);

  wire alu_1_is, alu_1_is_2, branch_unit_1_isbranchtaken, Clock_, control_unit_1_isimmediate,
       control_unit_1_isret, DataLock, flags_1_flags_e, flags_1_flags_gt, isRet_q, isWb_q;
  wire [3:0] address_q, Control_2_q, Control_q, multiplexer_5_out, multiplexer_6_out, multiplexer_8_out;
  wire [6:0] control_unit_1_isubranch, data_2_q;
  wire [12:0] ALUsignals_q, control_unit_1_alusignals;
  wire [31:0] A_q, adder_1_out, adder_2_out, adder_3_out, alu_1_aluresult, aluResult_2_q, aluResult_4_q, B_q,
       bit_extender_1_out, Branch_Target_q, calculate_immediate_1_immx, Instruction_2_q, Instruction_3_q,
       Instruction_4_q, Instruction_q, ldResult_2_q, memory_unit_1_ldresult, multiplexer_1_out,
       multiplexer_2_out, multiplexer_3_out, multiplexer_4_out, multiplexer_7_out, op2_2_q, Op2_q, pC_3_q,
       pC_4_q, PC_5_q, PC_6_q, PC_q, register_file_1_readd1, register_file_1_readd2, rom_1_data,
       shifter_1_out;

  Clock Clock (.out(Clock_));
  Register #(.width(32)) PC (.D(PC_6_q), .Q(PC_q), .clk(Clock_));  // open: en, clr
  // Probe on pC_4_q
  // Probe on aluResult_4_q
  // Probe on ldResult_2_q
  Register #(.width(32)) Instruction (.D(Instruction_4_q), .Q(Instruction_q), .clk(Clock_));  // open: en, clr
  Register #(.width(32)) pC_3 (.D(PC_q), .Q(pC_3_q), .clk(Clock_));  // open: en, clr
  Register #(.width(32)) pC_4 (.D(pC_3_q), .Q(pC_4_q), .clk(Clock_));  // open: en, clr
  Register #(.width(32), .trigger("falling")) PC_5 (
    .D(multiplexer_1_out), .en(DataLock), .Q(PC_5_q), .clk(Clock_), .clr(Reset));
  assign bit_extender_1_out = {{5{Instruction_4_q[26]}}, Instruction_4_q[26:0]};  // Bit_Extender bit_extender_1
  Register #(.width(32)) Branch_Target (.D(adder_1_out), .Q(Branch_Target_q), .clk(Clock_));  // open: en, clr
  Register #(.width(32)) Instruction_2 (.D(Instruction_q), .Q(Instruction_2_q), .clk(Clock_));  // open: en, clr
  Register #(.width(32)) Instruction_3 (.D(Instruction_2_q), .Q(Instruction_3_q), .clk(Clock_));  // open: en, clr
  Multiplexer #(.width(32), .enable("false")) multiplexer_1 (
    .in0(adder_3_out), .in1(multiplexer_2_out), .out(multiplexer_1_out), .sel(branch_unit_1_isbranchtaken));
  Shifter #(.width(32)) shifter_1 (.in(bit_extender_1_out), .\dist (5'b00010), .out(shifter_1_out));
  Adder #(.width(32)) adder_1 (.a(shifter_1_out), .b(PC_6_q), .out(adder_1_out));  // open: cin, cout
  Register #(.width(1)) isRet (.D(control_unit_1_isret), .Q(isRet_q), .clk(Clock_));  // open: en, clr
  Multiplexer #(.width(32), .enable("false")) multiplexer_2 (
    .in0(Branch_Target_q), .in1(A_q), .out(multiplexer_2_out), .sel(isRet_q));
  ALU alu_1 (
    .A(A_q), .B(B_q), .ALUsignals(ALUsignals_q), .aluResult(alu_1_aluresult), .is(alu_1_is), .is_2(alu_1_is_2));
  Register #(.width(32)) aluResult_2 (.D(alu_1_aluresult), .Q(aluResult_2_q), .clk(Clock_));  // open: en, clr
  Adder #(.width(32)) adder_2 (.a(pC_4_q), .b(32'h4), .out(adder_2_out));  // open: cin, cout
  // Probe on multiplexer_3_out
  Adder #(.width(32)) adder_3 (.a(32'h4), .b(PC_5_q), .out(adder_3_out));  // open: cin, cout
  Register #(.width(32)) PC_6 (.D(PC_5_q), .en(DataLock), .Q(PC_6_q), .clk(Clock_));  // open: clr
  Calculate_Immediate calculate_immediate_1 (.imm(Instruction_4_q[17:0]), .immx(calculate_immediate_1_immx));
  Register #(.width(32)) A (.D(register_file_1_readd1), .Q(A_q), .clk(Clock_));  // open: en, clr
  // Probe on aluResult_2_q
  Register #(.width(32)) ldResult_2 (.D(memory_unit_1_ldresult), .Q(ldResult_2_q), .clk(Clock_));  // open: en, clr
  Multiplexer #(.select(2), .width(32), .enable("false")) multiplexer_3 (
    .in0(aluResult_4_q), .in1(ldResult_2_q), .in2(adder_2_out), .out(multiplexer_3_out),
    .sel({Control_2_q[0], Control_2_q[2]}));  // open: in3
  Multiplexer #(.width(32), .enable("false")) multiplexer_4 (
    .in0(register_file_1_readd2), .in1(calculate_immediate_1_immx), .out(multiplexer_4_out),
    .sel(control_unit_1_isimmediate));
  Register #(.width(32)) B (.D(multiplexer_4_out), .Q(B_q), .clk(Clock_));  // open: en, clr
  // Probe on A_q
  // Probe on B_q
  Flags flags_1 (
    .isCmp(ALUsignals_q[0]), .is(alu_1_is), .is_2(alu_1_is_2), .flags_GT(flags_1_flags_gt),
    .flags_E(flags_1_flags_e));
  Memory_Unit memory_unit_1 (
    .MAR(aluResult_2_q), .ldResult(memory_unit_1_ldresult), .MDR(op2_2_q), .isSt(Control_q[1]),
    .isLd(Control_q[2]), .Clock(Clock_), .Reset(Reset));
  ROM #(.addrWidth(24), .dataWidth(32)) rom_1 (.addr(PC_5_q[25:2]), .data(rom_1_data), .sel(1'b1));
  Multiplexer #(.width(4), .enable("false")) multiplexer_5 (
    .in0(Instruction_4_q[17:14]), .in1(Instruction_4_q[25:22]), .out(multiplexer_5_out),
    .sel(control_unit_1_isubranch[4]));
  Multiplexer #(.width(4), .enable("false")) multiplexer_6 (
    .in0(Instruction_4_q[21:18]), .in1(4'b1111), .out(multiplexer_6_out), .sel(control_unit_1_isret));
  Register #(.width(32)) aluResult_4 (.D(aluResult_2_q), .Q(aluResult_4_q), .clk(Clock_));  // open: en, clr
  Register_File register_file_1 (
    .ReadA1(multiplexer_6_out), .ReadA2(multiplexer_5_out), .WriteE(isWb_q), .WriteD(out_4),
    .ReadD1(register_file_1_readd1), .ReadD2(register_file_1_readd2), .Clock(Clock_), .Reset(Reset),
    .DisplayD(Display), .DisplayA(Display_Address), .WriteA(address_q));
  Register #(.width(32)) Op2 (.D(register_file_1_readd2), .Q(Op2_q), .clk(Clock_));  // open: en, clr
  Branch_Unit branch_unit_1 (
    .isBeq(data_2_q[2]), .isUBranch(data_2_q[0]), .flags_E(flags_1_flags_e), .isBgt(data_2_q[1]),
    .flags_GT(flags_1_flags_gt), .isBranchTaken(branch_unit_1_isbranchtaken));
  Multiplexer #(.width(32), .enable("false")) multiplexer_7 (
    .in0(rom_1_data), .in1(32'h68000000), .out(multiplexer_7_out), .sel(1'b0));
  Control_Unit control_unit_1 (
    .isSt(control_unit_1_isubranch[4]), .isLd(control_unit_1_isubranch[5]),
    .isBeq(control_unit_1_isubranch[2]), .isBgt(control_unit_1_isubranch[1]), .isRet(control_unit_1_isret),
    .I_bit(Instruction_4_q[26]), .isImmediate(control_unit_1_isimmediate), .opcode(Instruction_4_q[31:27]),
    .isWb(control_unit_1_isubranch[6]), .isUbranch(control_unit_1_isubranch[0]),
    .isCall(control_unit_1_isubranch[3]), .ALUsignals(control_unit_1_alusignals));
  Register #(.width(13)) ALUsignals (.D(control_unit_1_alusignals), .Q(ALUsignals_q), .clk(Clock_));  // open: en, clr
  Multiplexer #(.width(4), .enable("false")) multiplexer_8 (
    .in0(Instruction_3_q[25:22]), .in1(4'b1111), .out(multiplexer_8_out), .sel(Control_2_q[0]));
  Register #(.width(32)) Instruction_4 (
    .D(multiplexer_7_out), .en(DataLock), .Q(Instruction_4_q), .clk(Clock_));  // open: clr
  Register #(.width(32)) op2_2 (.D(Op2_q), .Q(op2_2_q), .clk(Clock_));  // open: en, clr
  not not_1 (DataLock, Data_Lock);
  Register #(.width(7)) data_2 (.D(control_unit_1_isubranch), .Q(data_2_q), .clk(Clock_));  // open: en, clr
  Register #(.width(4)) Control (.D(data_2_q[6:3]), .Q(Control_q), .clk(Clock_));  // open: en, clr
  Register #(.width(32)) data_3 (.D(multiplexer_3_out), .Q(out_4), .clk(Clock_));  // open: en, clr
  Register #(.width(4)) Control_2 (.D(Control_q), .Q(Control_2_q), .clk(Clock_));  // open: en, clr
  Register #(.width(4)) address (.D(multiplexer_8_out), .Q(address_q), .clk(Clock_));  // open: en, clr
  Register #(.width(1)) isWb (.D(Control_2_q[3]), .Q(isWb_q), .clk(Clock_));  // open: en, clr
  // Probe on rom_1_data
  // Probe on Instruction_4_q
  // Probe on Instruction_2_q
  // Probe on out_4
  // Probe on Instruction_q
  // Probe on Instruction_3_q

  // Notes on the sheet:
  //   OF Stage
  //   EX Stage
  //   MA Stage
  //   RW Stage
  //   IF Stage
  //   IF-OF Register 
  //   OF-EX Registers
  //   EX-MA Registers
  //   MA-RW Registers
  //   f stands for ra(15)
  //   pc
  //   branchTarget
  //   B
  //   pc
  //   imm
  //   offset
  //   isRet
  //   isRet
  //   A
  //   ALU
  //   aluResult
  //   MAR
  //   isBranchTaken
  //   pc+4
  //   branchTarget
  //   calc immx
  //   immx
  //   is>
  //   is=
  //   isCmp
  //   MDR
  //   Memory
  //   Unit
  //   ldResult
  //   data
  //   Pipelined Processor
  //   -----------------------------------------------------------------------------------------------------------------------------------------------------------------------------------------------------------------------------------------------------------------------------------------------------------------------------------------------------------------------------------------
  //   -------------------------------------------------------------------------------------------------------------------------------------------------------------------------------------------------------------------------------------------------------------------------------------------------------------------------------------------------------------------------------------
  //   -----------------------------------------------------------------------------------------------------------------------------------------------------------------------------------------------------------------------------------------------------------------------------------------------------------------------------------------------------------------------------------
  //   instruction
  //   rs2
  //   isSt
  //   isImmediate
  //   -----------------------------------------------------------------------------------------------------------------------------------------------------------------------------------------------------------------------------------------------------------------------------------------------------------------------------------------------------------------------------------------
  //   -------------------------------------------------------------------------------------------------------------------------------------------------------------------------------------------------------------------------------------------------------------------------------------------------------------------------------------------------------------------------------------------
  //   flags(GT)
  //   Flags
  //   flags(E)
  //   -------------------------------------------------------------------------------------------------------------------------------------------------------------------------------------------------------------------------------------------------------------------------------------------------------------------------------------------------------------------------------------------
  //   -------------------------------------------------------------------------------------------------------------------------------------------------------------------------------------------------------------------------------------------------------------------------------------------------------------------------------------------------------------------------------------------
  //   isLd
  //   isSt
  //   -------------------------------------------------------------------------------------------------------------------------------------------------------------------------------------------------------------------------------------------------------------------------------------------------------------------------------------------------------------------------------------------
  //   -------------------------------------------------------------------------------------------------------------------------------------------------------------------------------------------------------------------------------------------------------------------------------------------------------------------------------------------------------------------------------------------
  //   isLd
  //   isCall
  //   Instruction Memory
  //   contents of rom_1 (hex, n*v repeats v):
  //   4c800003 4cc00004 4d000005 4d400006 4d800007 4e000008 1c8c000 4c800006 4cc00008 4d00000a 4d40000c
  //   4d80000e 4e000010 1c8c000
  //   nop
  //   rs1
  //   rd
  //   Register
  //   File
  //   op1
  //   op2
  //   Branch
  //   Unit
  //   ------------------------------------------------------------------------------------------------------------------------------------------------------------------------------------------------------------------------------------------------------------------------------------------------------------------------------------------------------------------------------------------------------------------
  //   isRet
  //   isWb
  //   E
  //   address
  //   A
  //   data
  //   D
  //   isBranchTaken
  //   rd
  //   opcode
  //   I bit
  //   ALUsignals
  //   isBeq
  //   isBgt
  //   isUBranch
  //   CONTROL
  //   UNIT
  //   isWb
  //   isLd
  //   isSt
  //   isWb
  //   address
  //   data
  //   isCall
  //   isBeq
  //   isBgt
  //   isWb
  //   isLd
  //   1. Disable PC, IF and IF-OF clock.
  //   2. Insert nop into EX stage
  //   isUBranch
  //   isCall
  //   isSt
  //   Data Lock
  //   isCall
  //   isLd
endmodule
